# Fritzing sketch Configure_HC-06 (saved by Fritzing 0.9.2b)
breadboards: 1

parts:
  Componente1 = Arduino Nano (Rev3.0) (ICSP)
  Componente2 = Bluetooth HC-06

nets:
  GND: Componente1.GND, Componente2.GND
  N1: Componente1.D2, Componente2.TXD
  N2: Componente1.D7, Componente2.RXD
  3V3: Componente1.3V3, Componente2.VCC
