# Fritzing sketch DrawingRobot (saved by Fritzing 0.9.2b)
breadboards: 1

parts:
  Componente1 = Arduino Nano (Rev3.0) (ICSP)
  Componente2 = Bluetooth HC-06
  VCC1 = Battery
  VCC2 = Battery
  J1 = Basic Servo
  X1 = X113647 Stepper Driver Board [package=board]
  MOTOR1 = 28BYJ-48 Stepper Motor
  X3 = X113647 Stepper Driver Board [package=board]
  MOTOR3 = 28BYJ-48 Stepper Motor

nets:
  N1: Componente1.D1/TX, Componente2.RXD
  N2: Componente1.D0/RX, Componente2.TXD
  GND: Componente1.GND, Componente2.GND, VCC2.-, J1.gnd, X1.GND, X3.GND
  N3: Componente1.D3, X3.IN4
  N4: Componente1.D4, X3.IN3
  N5: Componente1.D5, X3.IN2
  N6: Componente1.D6, X3.IN1
  N7: Componente1.D8, J1.pulse
  N8: Componente1.D10, X1.IN4
  N9: Componente1.D11/MOSI, X1.IN3
  N10: Componente1.D12/MISO, X1.IN2
  VCC: Componente1.VIN, Componente2.VCC, VCC1.+, J1.vcc, X1.+V, X3.+V
  N11: Componente1.D13/SCK, X1.IN1
  N12: VCC1.-, VCC2.+
  N13: X1.BLUE, MOTOR1.BLUE
  N14: X1.PINK, MOTOR1.PINK
  N15: X1.YELLOW, MOTOR1.YELLOW
  N16: X1.ORANGE, MOTOR1.ORANGE
  N17: X1.RED, MOTOR1.RED
  N18: X3.BLUE, MOTOR3.BLUE
  N19: X3.PINK, MOTOR3.PINK
  N20: X3.YELLOW, MOTOR3.YELLOW
  N21: X3.ORANGE, MOTOR3.ORANGE
  N22: X3.RED, MOTOR3.RED

custom parts:
  X113647 Stepper Driver Board: A common stepper motor driver board based on ULN2003APG darlington array
  28BYJ-48 Stepper Motor: 28BYJ-48 gear-reduction stepper motor (small)
